// Logisim project hack.circ as structural Verilog: 16 circuits, main circuit main
module main (
  input  M3,
  input  M2,
  input  M1,
  input  M0,
  output out_5,
  output [3:0] out_6,
  output [3:0] out_7
);

  wire encoder_1_encoder_o, piso_1_piso_o;

  PISO piso_1 (.M3(M3), .M2(M2), .M1(M1), .M0(M0), .E(1'b0), .R(1'b0), .piso_o(piso_1_piso_o));
  encoder encoder_1 (.encoder_in(piso_1_piso_o), .E(1'b0), .encoder_o(encoder_1_encoder_o));
  noisy_channel noisy_channel_1 (.ip(encoder_1_encoder_o), .op(out_5), .seq_PN(out_6), .upCounter(out_7));
endmodule

module encoder (
  input  encoder_in,
  input  E,
  output encoder_o
);

  wire and_1_out, and_2_out, clock_1_out, d_ff_1_q, d_ff_2_q, d_ff_3_q, not_1_out, or_1_out, xor_1_out,
       xor_2_out;

  Clock clock_1 (.out(clock_1_out));
  D_Flip_Flop d_ff_1 (.D(encoder_in), .clk(clock_1_out), .Q(d_ff_1_q));  // open: Qn, preset, reset
  D_Flip_Flop d_ff_2 (.D(d_ff_1_q), .clk(clock_1_out), .Q(d_ff_2_q));  // open: Qn, preset, reset
  // Probe on xor_1_out
  xor xor_1 (xor_1_out, encoder_in, d_ff_2_q);
  // Probe on xor_2_out
  ExactlyOne xor_2 (.out(xor_2_out), .in0(d_ff_2_q), .in1(d_ff_1_q), .in2(encoder_in));
  not not_1 (not_1_out, E);
  D_Flip_Flop d_ff_3 (.D(xor_1_out), .clk(clock_1_out), .Q(d_ff_3_q), .reset(1'b0));  // open: Qn, preset
  and and_1 (and_1_out, d_ff_3_q, E);
  and and_2 (and_2_out, not_1_out, xor_2_out);
  or or_1 (or_1_out, and_1_out, and_2_out);
  D_Flip_Flop d_ff_4 (.D(or_1_out), .clk(clock_1_out), .Q(encoder_o), .reset(1'b0));  // open: Qn, preset
endmodule

module PISO (
  input  M3,
  input  M2,
  input  M1,
  input  M0,
  input  E,
  input  R,
  output piso_o
);

  wire and_1_out, and_2_out, and_3_out, and_4_out, and_5_out, and_6_out, clock_1_out, d_ff_1_q, d_ff_2_q,
       d_ff_3_q, not_1_out, or_1_out, or_2_out, or_3_out;

  not not_1 (not_1_out, E);
  Clock clock_1 (.out(clock_1_out));
  D_Flip_Flop d_ff_1 (.D(M3), .clk(clock_1_out), .Q(d_ff_1_q), .reset(R));  // open: Qn, preset
  and and_1 (and_1_out, d_ff_1_q, E);
  and and_2 (and_2_out, not_1_out, M2);
  or or_1 (or_1_out, and_1_out, and_2_out);
  D_Flip_Flop d_ff_2 (.D(or_1_out), .clk(clock_1_out), .Q(d_ff_2_q), .reset(R));  // open: Qn, preset
  and and_3 (and_3_out, d_ff_2_q, E);
  and and_4 (and_4_out, not_1_out, M1);
  or or_2 (or_2_out, and_3_out, and_4_out);
  D_Flip_Flop d_ff_3 (.D(or_2_out), .clk(clock_1_out), .Q(d_ff_3_q), .reset(R));  // open: Qn, preset
  and and_5 (and_5_out, d_ff_3_q, E);
  and and_6 (and_6_out, not_1_out, M0);
  or or_3 (or_3_out, and_5_out, and_6_out);
  D_Flip_Flop d_ff_4 (.D(or_3_out), .clk(clock_1_out), .Q(piso_o), .reset(R));  // open: Qn, preset
endmodule

module PN_Seq (
  input  en,
  output q3,
  output q2,
  output q1,
  output q0
);

  wire and_1_out, and_2_out, and_3_out, and_4_out, and_5_out, and_6_out, and_7_out, and_8_out, and_9_out,
       and_10_out, and_11_out, and_12_out, and_13_out, and_14_out, clk_out, not_1_out, not_2_out, not_3_out,
       not_4_out, or_1_out, or_2_out, or_3_out, or_4_out, or_5_out;

  not not_1 (not_1_out, q3);
  not not_2 (not_2_out, q2);
  not not_3 (not_3_out, q1);
  not not_4 (not_4_out, q0);
  and and_1 (and_1_out, q3, not_3_out);
  and and_2 (and_2_out, q2, q1, not_4_out);
  and and_3 (and_3_out, not_1_out, not_2_out, q1, q0);
  or or_1 (or_1_out, and_1_out, and_2_out, and_3_out);
  Clock clk (.out(clk_out));
  D_Flip_Flop A (.D(or_1_out), .clk(and_4_out), .Q(q3));  // open: Qn, preset, reset
  and and_4 (and_4_out, clk_out, en);
  and and_5 (and_5_out, q3, q1);
  and and_6 (and_6_out, not_1_out, not_2_out, not_4_out);
  and and_7 (and_7_out, not_2_out, not_3_out, q0);
  and and_8 (and_8_out, not_2_out, q1, not_4_out);
  and and_9 (and_9_out, q3, not_3_out);
  and and_10 (and_10_out, q2, not_3_out, not_4_out);
  and and_11 (and_11_out, q2, not_3_out);
  and and_12 (and_12_out, not_2_out, q1, q0);
  and and_13 (and_13_out, not_1_out, not_2_out, q1);
  and and_14 (and_14_out, q3, not_3_out, not_4_out);
  or or_2 (or_2_out, and_5_out, and_6_out);
  or or_3 (or_3_out, and_7_out, and_8_out, and_9_out);
  or or_4 (or_4_out, and_11_out, and_12_out, and_13_out, and_14_out);
  D_Flip_Flop B (.D(or_2_out), .clk(and_4_out), .Q(q2));  // open: Qn, preset, reset
  or or_5 (or_5_out, or_3_out, and_10_out);
  D_Flip_Flop C (.D(or_5_out), .clk(and_4_out), .Q(q1));  // open: Qn, preset, reset
  D_Flip_Flop D (.D(or_4_out), .clk(and_4_out), .Q(q0));  // open: Qn, preset, reset

  // Notes on the sheet:
  //   A
  //   B
  //   C
  //   D
endmodule

module noisy_channel (
  input  ip,
  output op,
  output [3:0] seq_PN,
  output [3:0] upCounter
);

  wire clock_1_out, comp_1_op, d_ff_1_q, not_1_out;

  upcon upcon_1 (.R(d_ff_1_q), .q0(upCounter[0]), .q1(upCounter[1]), .q2(upCounter[2]), .q3(upCounter[3]));
  not not_1 (not_1_out, ip);
  PN_Seq pn_seq_1 (.en(d_ff_1_q), .q3(seq_PN[3]), .q2(seq_PN[2]), .q1(seq_PN[1]), .q0(seq_PN[0]));
  comp comp_1 (
    .p3(seq_PN[3]), .p2(seq_PN[2]), .p1(seq_PN[1]), .p0(seq_PN[0]), .u0(upCounter[0]), .u1(upCounter[1]),
    .u2(upCounter[2]), .u3(upCounter[3]), .op(comp_1_op));
  mux mux_1 (.A(ip), .B(not_1_out), .S(d_ff_1_q), .op(op));
  D_Flip_Flop d_ff_1 (.D(comp_1_op), .clk(clock_1_out), .Q(d_ff_1_q));  // open: Qn, preset, reset
  Clock clock_1 (.out(clock_1_out));
endmodule

module mux (
  input  A,
  input  B,
  input  S,
  output op
);

  wire and_1_out, and_2_out, not_1_out;

  not not_1 (not_1_out, S);
  and and_1 (and_1_out, A, not_1_out);
  and and_2 (and_2_out, S, B);
  or or_1 (op, and_1_out, and_2_out);
endmodule

module comp (
  input  p3,
  input  p2,
  input  p1,
  input  p0,
  input  u0,
  input  u1,
  input  u2,
  input  u3,
  output op
);

  wire xnor_1_out, xnor_2_out, xnor_3_out, xnor_4_out;

  xnor xnor_1 (xnor_1_out, p0, u0);
  xnor xnor_2 (xnor_2_out, p1, u1);
  xnor xnor_3 (xnor_3_out, p2, u2);
  xnor xnor_4 (xnor_4_out, p3, u3);
  and and_1 (op, xnor_1_out, xnor_2_out, xnor_3_out, xnor_4_out);
endmodule

module upcon (
  input  R,
  output q0,
  output q1,
  output q2,
  output q3
);

  wire and_1_out, and_2_out, clock_1_out;

  Clock clock_1 (.out(clock_1_out));
  J_K_Flip_Flop j_k_ff_1 (.J(1'b1), .K(1'b1), .clk(clock_1_out), .Q(q0), .reset(R));  // open: Qn, preset
  J_K_Flip_Flop j_k_ff_2 (.J(q0), .K(q0), .clk(clock_1_out), .Q(q1), .reset(R));  // open: Qn, preset
  and and_1 (and_1_out, q0, q1);
  J_K_Flip_Flop j_k_ff_3 (.J(and_1_out), .K(and_1_out), .clk(clock_1_out), .Q(q2), .reset(R));  // open: Qn, preset
  and and_2 (and_2_out, and_1_out, q2);
  J_K_Flip_Flop j_k_ff_4 (.J(and_2_out), .K(and_2_out), .clk(clock_1_out), .Q(q3), .reset(R));  // open: Qn, preset
endmodule

module BMU (
  input  C0,
  input  C1,
  input  C2,
  input  D0,
  input  D1,
  input  D2,
  output Q0,
  output Q1,
  output Q2
);

  wire clock_1_out, t_ff_1_q, t_ff_2_q, t_ff_3_q, xor_1_out, xor_2_out, xor_3_out;

  xor xor_1 (xor_1_out, C0, D0);
  Clock clock_1 (.out(clock_1_out));
  xor xor_2 (xor_2_out, C1, D1);
  xor xor_3 (xor_3_out, C2, D2);
  T_Flip_Flop t_ff_1 (.T(xor_1_out), .clk(clock_1_out), .Q(t_ff_1_q));  // open: Qn, reset, preset
  T_Flip_Flop t_ff_2 (.T(xor_2_out), .clk(clock_1_out), .Q(t_ff_2_q));  // open: Qn, reset, preset
  T_Flip_Flop t_ff_3 (.T(xor_3_out), .clk(clock_1_out), .Q(t_ff_3_q));  // open: Qn, reset, preset
endmodule

module SMU (
  input  PM0_S0,
  input  PM1_S0,
  input  PM2_S0,
  input  PM3_S0,
  input  PM0_S1,
  input  PM1_S1,
  input  PM2_S1,
  input  PM3_S1,
  input  PM0_S2,
  input  PM1_S2,
  input  PM2_S2,
  input  PM3_S2,
  input  PM0_S3,
  input  PM1_S3,
  input  PM2_S3,
  input  PM3_S3,
  output out_17,
  output out_18,
  output out_19,
  output out_20,
  output out_21,
  output out_22,
  output out_23,
  output out_24,
  output out_25,
  output out_26,
  output out_27,
  output out_28,
  output out_29,
  output out_30,
  output out_31,
  output out_32
);

  wire clock_1_out, d_ff_1_q, d_ff_2_q, d_ff_3_q, d_ff_4_q, d_ff_5_q, d_ff_6_q, d_ff_7_q, d_ff_8_q, d_ff_9_q,
       d_ff_10_q, d_ff_11_q, d_ff_12_q, d_ff_13_q, d_ff_14_q, d_ff_15_q, d_ff_16_q, d_ff_17_q, d_ff_18_q,
       d_ff_19_q, d_ff_20_q, d_ff_21_q, d_ff_22_q, d_ff_23_q, d_ff_24_q, d_ff_25_q, d_ff_26_q, d_ff_27_q,
       d_ff_28_q, d_ff_29_q, d_ff_30_q, d_ff_31_q, d_ff_32_q, d_ff_33_q, d_ff_34_q, d_ff_35_q, d_ff_36_q,
       d_ff_37_q, d_ff_38_q, d_ff_39_q, d_ff_40_q, d_ff_41_q, d_ff_42_q, d_ff_43_q, d_ff_44_q, d_ff_45_q,
       d_ff_46_q, d_ff_47_q, d_ff_48_q, d_ff_49_q, d_ff_50_q, d_ff_51_q, d_ff_52_q, d_ff_53_q, d_ff_54_q,
       d_ff_55_q, d_ff_56_q, d_ff_57_q, d_ff_58_q, d_ff_59_q, d_ff_60_q, d_ff_61_q, d_ff_62_q, d_ff_63_q,
       d_ff_64_q, d_ff_65_q, d_ff_66_q, d_ff_67_q, d_ff_68_q, d_ff_69_q, d_ff_70_q, d_ff_71_q, d_ff_72_q,
       d_ff_73_q, d_ff_74_q, d_ff_75_q, d_ff_76_q, d_ff_77_q, d_ff_78_q, d_ff_79_q, d_ff_80_q;

  Clock clock_1 (.out(clock_1_out));
  D_Flip_Flop d_ff_1 (.D(PM0_S0), .clk(clock_1_out), .Q(d_ff_1_q));  // open: Qn, preset, reset
  D_Flip_Flop d_ff_2 (.D(PM1_S0), .clk(clock_1_out), .Q(d_ff_2_q));  // open: Qn, preset, reset
  D_Flip_Flop d_ff_3 (.D(PM2_S0), .clk(clock_1_out), .Q(d_ff_3_q));  // open: Qn, preset, reset
  D_Flip_Flop d_ff_4 (.D(PM3_S0), .clk(clock_1_out), .Q(d_ff_4_q));  // open: Qn, preset, reset
  D_Flip_Flop d_ff_5 (.D(PM0_S1), .clk(clock_1_out), .Q(d_ff_5_q));  // open: Qn, preset, reset
  D_Flip_Flop d_ff_6 (.D(PM1_S1), .clk(clock_1_out), .Q(d_ff_6_q));  // open: Qn, preset, reset
  D_Flip_Flop d_ff_7 (.D(PM2_S1), .clk(clock_1_out), .Q(d_ff_7_q));  // open: Qn, preset, reset
  D_Flip_Flop d_ff_8 (.D(PM3_S1), .clk(clock_1_out), .Q(d_ff_8_q));  // open: Qn, preset, reset
  D_Flip_Flop d_ff_9 (.D(PM0_S2), .clk(clock_1_out), .Q(d_ff_9_q));  // open: Qn, preset, reset
  D_Flip_Flop d_ff_10 (.D(PM1_S2), .clk(clock_1_out), .Q(d_ff_10_q));  // open: Qn, preset, reset
  D_Flip_Flop d_ff_11 (.D(PM2_S2), .clk(clock_1_out), .Q(d_ff_11_q));  // open: Qn, preset, reset
  D_Flip_Flop d_ff_12 (.D(PM3_S2), .clk(clock_1_out), .Q(d_ff_12_q));  // open: Qn, preset, reset
  D_Flip_Flop d_ff_13 (.D(PM0_S3), .clk(clock_1_out), .Q(d_ff_13_q));  // open: Qn, preset, reset
  D_Flip_Flop d_ff_14 (.D(PM1_S3), .clk(clock_1_out), .Q(d_ff_14_q));  // open: Qn, preset, reset
  D_Flip_Flop d_ff_15 (.D(PM2_S3), .clk(clock_1_out), .Q(d_ff_15_q));  // open: Qn, preset, reset
  D_Flip_Flop d_ff_16 (.D(PM3_S3), .clk(clock_1_out), .Q(d_ff_16_q));  // open: Qn, preset, reset
  D_Flip_Flop d_ff_17 (.D(d_ff_1_q), .clk(clock_1_out), .Q(d_ff_17_q));  // open: Qn, preset, reset
  D_Flip_Flop d_ff_18 (.D(d_ff_2_q), .clk(clock_1_out), .Q(d_ff_18_q));  // open: Qn, preset, reset
  D_Flip_Flop d_ff_19 (.D(d_ff_3_q), .clk(clock_1_out), .Q(d_ff_19_q));  // open: Qn, preset, reset
  D_Flip_Flop d_ff_20 (.D(d_ff_4_q), .clk(clock_1_out), .Q(d_ff_20_q));  // open: Qn, preset, reset
  D_Flip_Flop d_ff_21 (.D(d_ff_5_q), .clk(clock_1_out), .Q(d_ff_21_q));  // open: Qn, preset, reset
  D_Flip_Flop d_ff_22 (.D(d_ff_6_q), .clk(clock_1_out), .Q(d_ff_22_q));  // open: Qn, preset, reset
  D_Flip_Flop d_ff_23 (.D(d_ff_7_q), .clk(clock_1_out), .Q(d_ff_23_q));  // open: Qn, preset, reset
  D_Flip_Flop d_ff_24 (.D(d_ff_8_q), .clk(clock_1_out), .Q(d_ff_24_q));  // open: Qn, preset, reset
  D_Flip_Flop d_ff_25 (.D(d_ff_9_q), .clk(clock_1_out), .Q(d_ff_25_q));  // open: Qn, preset, reset
  D_Flip_Flop d_ff_26 (.D(d_ff_10_q), .clk(clock_1_out), .Q(d_ff_26_q));  // open: Qn, preset, reset
  D_Flip_Flop d_ff_27 (.D(d_ff_11_q), .clk(clock_1_out), .Q(d_ff_27_q));  // open: Qn, preset, reset
  D_Flip_Flop d_ff_28 (.D(d_ff_12_q), .clk(clock_1_out), .Q(d_ff_28_q));  // open: Qn, preset, reset
  D_Flip_Flop d_ff_29 (.D(d_ff_13_q), .clk(clock_1_out), .Q(d_ff_29_q));  // open: Qn, preset, reset
  D_Flip_Flop d_ff_30 (.D(d_ff_14_q), .clk(clock_1_out), .Q(d_ff_30_q));  // open: Qn, preset, reset
  D_Flip_Flop d_ff_31 (.D(d_ff_15_q), .clk(clock_1_out), .Q(d_ff_31_q));  // open: Qn, preset, reset
  D_Flip_Flop d_ff_32 (.D(d_ff_16_q), .clk(clock_1_out), .Q(d_ff_32_q));  // open: Qn, preset, reset
  D_Flip_Flop d_ff_33 (.D(d_ff_17_q), .clk(clock_1_out), .Q(d_ff_33_q));  // open: Qn, preset, reset
  D_Flip_Flop d_ff_34 (.D(d_ff_18_q), .clk(clock_1_out), .Q(d_ff_34_q));  // open: Qn, preset, reset
  D_Flip_Flop d_ff_35 (.D(d_ff_19_q), .clk(clock_1_out), .Q(d_ff_35_q));  // open: Qn, preset, reset
  D_Flip_Flop d_ff_36 (.D(d_ff_20_q), .clk(clock_1_out), .Q(d_ff_36_q));  // open: Qn, preset, reset
  D_Flip_Flop d_ff_37 (.D(d_ff_21_q), .clk(clock_1_out), .Q(d_ff_37_q));  // open: Qn, preset, reset
  D_Flip_Flop d_ff_38 (.D(d_ff_22_q), .clk(clock_1_out), .Q(d_ff_38_q));  // open: Qn, preset, reset
  D_Flip_Flop d_ff_39 (.D(d_ff_23_q), .clk(clock_1_out), .Q(d_ff_39_q));  // open: Qn, preset, reset
  D_Flip_Flop d_ff_40 (.D(d_ff_24_q), .clk(clock_1_out), .Q(d_ff_40_q));  // open: Qn, preset, reset
  D_Flip_Flop d_ff_41 (.D(d_ff_25_q), .clk(clock_1_out), .Q(d_ff_41_q));  // open: Qn, preset, reset
  D_Flip_Flop d_ff_42 (.D(d_ff_26_q), .clk(clock_1_out), .Q(d_ff_42_q));  // open: Qn, preset, reset
  D_Flip_Flop d_ff_43 (.D(d_ff_27_q), .clk(clock_1_out), .Q(d_ff_43_q));  // open: Qn, preset, reset
  D_Flip_Flop d_ff_44 (.D(d_ff_28_q), .clk(clock_1_out), .Q(d_ff_44_q));  // open: Qn, preset, reset
  D_Flip_Flop d_ff_45 (.D(d_ff_29_q), .clk(clock_1_out), .Q(d_ff_45_q));  // open: Qn, preset, reset
  D_Flip_Flop d_ff_46 (.D(d_ff_30_q), .clk(clock_1_out), .Q(d_ff_46_q));  // open: Qn, preset, reset
  D_Flip_Flop d_ff_47 (.D(d_ff_31_q), .clk(clock_1_out), .Q(d_ff_47_q));  // open: Qn, preset, reset
  D_Flip_Flop d_ff_48 (.D(d_ff_32_q), .clk(clock_1_out), .Q(d_ff_48_q));  // open: Qn, preset, reset
  D_Flip_Flop d_ff_49 (.D(d_ff_33_q), .clk(clock_1_out), .Q(d_ff_49_q));  // open: Qn, preset, reset
  D_Flip_Flop d_ff_50 (.D(d_ff_34_q), .clk(clock_1_out), .Q(d_ff_50_q));  // open: Qn, preset, reset
  D_Flip_Flop d_ff_51 (.D(d_ff_35_q), .clk(clock_1_out), .Q(d_ff_51_q));  // open: Qn, preset, reset
  D_Flip_Flop d_ff_52 (.D(d_ff_36_q), .clk(clock_1_out), .Q(d_ff_52_q));  // open: Qn, preset, reset
  D_Flip_Flop d_ff_53 (.D(d_ff_37_q), .clk(clock_1_out), .Q(d_ff_53_q));  // open: Qn, preset, reset
  D_Flip_Flop d_ff_54 (.D(d_ff_38_q), .clk(clock_1_out), .Q(d_ff_54_q));  // open: Qn, preset, reset
  D_Flip_Flop d_ff_55 (.D(d_ff_39_q), .clk(clock_1_out), .Q(d_ff_55_q));  // open: Qn, preset, reset
  D_Flip_Flop d_ff_56 (.D(d_ff_40_q), .clk(clock_1_out), .Q(d_ff_56_q));  // open: Qn, preset, reset
  D_Flip_Flop d_ff_57 (.D(d_ff_41_q), .clk(clock_1_out), .Q(d_ff_57_q));  // open: Qn, preset, reset
  D_Flip_Flop d_ff_58 (.D(d_ff_42_q), .clk(clock_1_out), .Q(d_ff_58_q));  // open: Qn, preset, reset
  D_Flip_Flop d_ff_59 (.D(d_ff_43_q), .clk(clock_1_out), .Q(d_ff_59_q));  // open: Qn, preset, reset
  D_Flip_Flop d_ff_60 (.D(d_ff_44_q), .clk(clock_1_out), .Q(d_ff_60_q));  // open: Qn, preset, reset
  D_Flip_Flop d_ff_61 (.D(d_ff_45_q), .clk(clock_1_out), .Q(d_ff_61_q));  // open: Qn, preset, reset
  D_Flip_Flop d_ff_62 (.D(d_ff_46_q), .clk(clock_1_out), .Q(d_ff_62_q));  // open: Qn, preset, reset
  D_Flip_Flop d_ff_63 (.D(d_ff_47_q), .clk(clock_1_out), .Q(d_ff_63_q));  // open: Qn, preset, reset
  D_Flip_Flop d_ff_64 (.D(d_ff_48_q), .clk(clock_1_out), .Q(d_ff_64_q));  // open: Qn, preset, reset
  D_Flip_Flop d_ff_65 (.D(d_ff_49_q), .clk(clock_1_out), .Q(d_ff_65_q));  // open: Qn, preset, reset
  D_Flip_Flop d_ff_66 (.D(d_ff_50_q), .clk(clock_1_out), .Q(d_ff_66_q));  // open: Qn, preset, reset
  D_Flip_Flop d_ff_67 (.D(d_ff_51_q), .clk(clock_1_out), .Q(d_ff_67_q));  // open: Qn, preset, reset
  D_Flip_Flop d_ff_68 (.D(d_ff_52_q), .clk(clock_1_out), .Q(d_ff_68_q));  // open: Qn, preset, reset
  D_Flip_Flop d_ff_69 (.D(d_ff_53_q), .clk(clock_1_out), .Q(d_ff_69_q));  // open: Qn, preset, reset
  D_Flip_Flop d_ff_70 (.D(d_ff_54_q), .clk(clock_1_out), .Q(d_ff_70_q));  // open: Qn, preset, reset
  D_Flip_Flop d_ff_71 (.D(d_ff_55_q), .clk(clock_1_out), .Q(d_ff_71_q));  // open: Qn, preset, reset
  D_Flip_Flop d_ff_72 (.D(d_ff_56_q), .clk(clock_1_out), .Q(d_ff_72_q));  // open: Qn, preset, reset
  D_Flip_Flop d_ff_73 (.D(d_ff_57_q), .clk(clock_1_out), .Q(d_ff_73_q));  // open: Qn, preset, reset
  D_Flip_Flop d_ff_74 (.D(d_ff_58_q), .clk(clock_1_out), .Q(d_ff_74_q));  // open: Qn, preset, reset
  D_Flip_Flop d_ff_75 (.D(d_ff_59_q), .clk(clock_1_out), .Q(d_ff_75_q));  // open: Qn, preset, reset
  D_Flip_Flop d_ff_76 (.D(d_ff_60_q), .clk(clock_1_out), .Q(d_ff_76_q));  // open: Qn, preset, reset
  D_Flip_Flop d_ff_77 (.D(d_ff_61_q), .clk(clock_1_out), .Q(d_ff_77_q));  // open: Qn, preset, reset
  D_Flip_Flop d_ff_78 (.D(d_ff_62_q), .clk(clock_1_out), .Q(d_ff_78_q));  // open: Qn, preset, reset
  D_Flip_Flop d_ff_79 (.D(d_ff_63_q), .clk(clock_1_out), .Q(d_ff_79_q));  // open: Qn, preset, reset
  D_Flip_Flop d_ff_80 (.D(d_ff_64_q), .clk(clock_1_out), .Q(d_ff_80_q));  // open: Qn, preset, reset
  D_Flip_Flop d_ff_81 (.D(d_ff_65_q), .clk(clock_1_out), .Q(out_17));  // open: Qn, preset, reset
  D_Flip_Flop d_ff_82 (.D(d_ff_66_q), .clk(clock_1_out), .Q(out_18));  // open: Qn, preset, reset
  D_Flip_Flop d_ff_83 (.D(d_ff_67_q), .clk(clock_1_out), .Q(out_19));  // open: Qn, preset, reset
  D_Flip_Flop d_ff_84 (.D(d_ff_68_q), .clk(clock_1_out), .Q(out_20));  // open: Qn, preset, reset
  D_Flip_Flop d_ff_85 (.D(d_ff_69_q), .clk(clock_1_out), .Q(out_21));  // open: Qn, preset, reset
  D_Flip_Flop d_ff_86 (.D(d_ff_70_q), .clk(clock_1_out), .Q(out_22));  // open: Qn, preset, reset
  D_Flip_Flop d_ff_87 (.D(d_ff_71_q), .clk(clock_1_out), .Q(out_23));  // open: Qn, preset, reset
  D_Flip_Flop d_ff_88 (.D(d_ff_72_q), .clk(clock_1_out), .Q(out_24));  // open: Qn, preset, reset
  D_Flip_Flop d_ff_89 (.D(d_ff_73_q), .clk(clock_1_out), .Q(out_25));  // open: Qn, preset, reset
  D_Flip_Flop d_ff_90 (.D(d_ff_74_q), .clk(clock_1_out), .Q(out_26));  // open: Qn, preset, reset
  D_Flip_Flop d_ff_91 (.D(d_ff_75_q), .clk(clock_1_out), .Q(out_27));  // open: Qn, preset, reset
  D_Flip_Flop d_ff_92 (.D(d_ff_76_q), .clk(clock_1_out), .Q(out_28));  // open: Qn, preset, reset
  D_Flip_Flop d_ff_93 (.D(d_ff_77_q), .clk(clock_1_out), .Q(out_29));  // open: Qn, preset, reset
  D_Flip_Flop d_ff_94 (.D(d_ff_78_q), .clk(clock_1_out), .Q(out_30));  // open: Qn, preset, reset
  D_Flip_Flop d_ff_95 (.D(d_ff_79_q), .clk(clock_1_out), .Q(out_31));  // open: Qn, preset, reset
  D_Flip_Flop d_ff_96 (.D(d_ff_80_q), .clk(clock_1_out), .Q(out_32));  // open: Qn, preset, reset
endmodule

module virtibi_decoder (
  input  in_1,
  input  in_2,
  input  in_3,
  input  in_4,
  input  in_5,
  input  in_6,
  input  in_7,
  input  in_8,
  input  in_9,
  input  in_10,
  input  in_11,
  input  in_12
);

  wire asc_1_op1, bmu_1_q0, bmu_1_q1, bmu_1_q2, bmu_2_q0, bmu_2_q1, bmu_2_q2, clock_1_out, d_ff_1_q,
       d_ff_2_q, d_ff_3_q;

  BMU bmu_1 (
    .C0(in_1), .C1(in_2), .C2(in_3), .D0(in_4), .D1(in_5), .D2(in_6), .Q0(bmu_1_q0), .Q1(bmu_1_q1),
    .Q2(bmu_1_q2));
  BMU bmu_2 (
    .C0(in_7), .C1(in_8), .C2(in_9), .D0(in_10), .D1(in_11), .D2(in_12), .Q0(bmu_2_q0), .Q1(bmu_2_q1),
    .Q2(bmu_2_q2));
  Clock clock_1 (.out(clock_1_out));
  ASC asc_1 (
    .q0_upper(bmu_1_q0), .q1_upper(bmu_1_q1), .q2_upper(bmu_1_q2), .pm0_upper(d_ff_1_q),
    .pm1_upper(d_ff_2_q), .pm2_upper(d_ff_3_q), .q0_lower(bmu_2_q0), .q1_lower(bmu_2_q1),
    .q2_lower(bmu_2_q2), .pm0_lower(d_ff_1_q), .pm1_lower(d_ff_2_q), .pm2_lower(d_ff_3_q), .op1(asc_1_op1),
    .op2(clock_1_out), .op3(clock_1_out));  // open: in_7, in_14, op4
  D_Flip_Flop d_ff_1 (.D(asc_1_op1), .clk(clock_1_out), .Q(d_ff_1_q));  // open: Qn, preset, reset
  D_Flip_Flop d_ff_2 (.D(clock_1_out), .clk(clock_1_out), .Q(d_ff_2_q));  // open: Qn, preset, reset
  D_Flip_Flop d_ff_3 (.D(clock_1_out), .clk(clock_1_out), .Q(d_ff_3_q));  // open: Qn, preset, reset
  SMU smu_1 ();  // open: PM0_S0, PM1_S0, PM2_S0, PM3_S0, PM0_S1, PM1_S1, PM2_S1, PM3_S1, PM0_S2, PM1_S2, PM2_S2, PM3_S2, PM0_S3, PM1_S3, PM2_S3, PM3_S3, out_17, out_18, out_19, out_20, out_21, out_22, out_23, out_24, out_25, out_26, out_27, out_28, out_29, out_30, out_31, out_32
endmodule

module ASC (
  input  q0_upper,
  input  q1_upper,
  input  q2_upper,
  input  pm0_upper,
  input  pm1_upper,
  input  pm2_upper,
  input  in_7,
  input  q0_lower,
  input  q1_lower,
  input  q2_lower,
  input  pm0_lower,
  input  pm1_lower,
  input  pm2_lower,
  input  in_14,
  output op1,
  output op2,
  output op3,
  output op4
);

  wire four_add_1_cout, four_add_1_s0, four_add_1_s1, four_add_1_s2, four_add_2_cout, four_add_2_s0,
       four_add_2_s1, four_add_2_s2, fourbitcomp_1_op, not_1_out;

  four_add four_add_1 (
    .a0(q0_upper), .a1(q1_upper), .a2(q2_upper), .b0(pm0_upper), .b1(pm1_upper), .b2(pm2_upper), .cin(in_7),
    .s0(four_add_1_s0), .s1(four_add_1_s1), .s2(four_add_1_s2), .cout(four_add_1_cout));
  four_add four_add_2 (
    .a0(q0_lower), .a1(q1_lower), .a2(q2_lower), .b0(pm0_lower), .b1(pm1_lower), .b2(pm2_lower), .cin(in_14),
    .s0(four_add_2_s0), .s1(four_add_2_s1), .s2(four_add_2_s2), .cout(four_add_2_cout));
  fourbitcomp fourbitcomp_1 (
    .a0(four_add_1_s0), .a1(four_add_1_s1), .a2(four_add_1_s2), .a3(four_add_1_cout), .b0(four_add_2_s0),
    .b1(four_add_2_s1), .b2(four_add_2_s2), .b3(four_add_2_cout), .op(fourbitcomp_1_op));
  not not_1 (not_1_out, fourbitcomp_1_op);
  mux21 mux21_1 (.i0(four_add_1_s0), .i1(four_add_2_s0), .sel(not_1_out), .op(op1));
  mux21 mux21_2 (.i0(four_add_1_s1), .i1(four_add_2_s1), .sel(not_1_out), .op(op2));
  mux21 mux21_3 (.i0(four_add_1_s2), .i1(four_add_2_s2), .sel(not_1_out), .op(op3));
  mux21 mux21_4 (.i0(four_add_1_cout), .i1(four_add_2_cout), .sel(not_1_out), .op(op4));
endmodule

module Full_Add (
  input  a,
  input  b,
  input  cin,
  output sum,
  output carry
);

  wire and_1_out, and_2_out, and_3_out, xor_1_out;

  xor xor_1 (xor_1_out, a, b);
  and and_1 (and_1_out, a, b);
  and and_2 (and_2_out, a, cin);
  and and_3 (and_3_out, b, cin);
  xor xor_2 (sum, xor_1_out, cin);
  or or_1 (carry, and_1_out, and_2_out, and_3_out);
endmodule

module fourbitcomp (
  input  a0,
  input  a1,
  input  a2,
  input  a3,
  input  b0,
  input  b1,
  input  b2,
  input  b3,
  output op
);

  wire and_1_out, and_2_out, and_3_out, and_4_out, and_5_out, not_1_out, not_2_out, or_1_out, xnor_1_out,
       xnor_2_out, xnor_3_out, xnor_4_out;

  not not_1 (not_1_out, b0);
  xnor xnor_1 (xnor_1_out, b0, a0);
  not not_2 (not_2_out, b1);
  and and_1 (and_1_out, not_1_out, a0);
  and and_2 (and_2_out, not_2_out, xnor_1_out, a1);
  xnor xnor_2 (xnor_2_out, b1, a1);
  not not_3 (xnor_2_out, b2);
  xnor xnor_3 (xnor_3_out, b2, a2);
  and and_3 (and_3_out, xnor_2_out, xnor_2_out, xnor_1_out, a2);
  not not_4 (xnor_1_out, b3);
  xnor xnor_4 (xnor_4_out, b3, a3);
  and and_4 (and_4_out, xnor_1_out, xnor_1_out, a3, xnor_2_out);
  and and_5 (and_5_out, xnor_1_out, xnor_2_out, xnor_3_out, xnor_4_out);
  or or_1 (or_1_out, and_1_out, and_2_out, and_3_out, and_4_out);
  nor nor_1 (op, and_5_out, or_1_out);
endmodule

module mux21 (
  input  i0,
  input  i1,
  input  sel,
  output op
);

  wire and_1_out, and_2_out, not_1_out;

  not not_1 (not_1_out, sel);
  and and_1 (and_1_out, i1, sel);
  and and_2 (and_2_out, not_1_out, i0);
  or or_1 (op, and_1_out, and_2_out);
endmodule

module four_add (
  input  a0,
  input  a1,
  input  a2,
  input  b0,
  input  b1,
  input  b2,
  input  cin,
  output s0,
  output s1,
  output s2,
  output cout
);

  wire full_add_1_carry, full_add_2_carry;

  Full_Add full_add_1 (.a(a0), .b(b0), .cin(cin), .sum(s0), .carry(full_add_1_carry));
  Full_Add full_add_2 (.a(a1), .b(b1), .cin(full_add_1_carry), .sum(s1), .carry(full_add_2_carry));
  Full_Add full_add_3 (.a(a2), .b(b2), .cin(full_add_2_carry), .sum(s2), .carry(cout));
endmodule
